# Fritzing sketch esp-01-programmer (saved by Fritzing 0.9.3b)

parts:
  U1 = ESP8266 WiFi Module [part_number=ESP8266]
  R1 = Resistor [tolerance=±5% resistance=4.7k package="0603 [SMD]"]
  S1 = Toggle Switch [package=THT]

nets:
  N1: U1.VCC, R1.Pin_0
  N2: U1.GPIO_0, S1.COM
  N3: U1.GND, S1.L2
  N4: R1.Pin_1, S1.L1

custom parts:
  ESP8266 WiFi Module: Generic WiFi Module based on the ESP8266 with onboard PCB antenna and UART communications
